# Fritzing sketch TemperatureMonitor_REV1 (saved by Fritzing 0.9.3b)
circuit board: 8.46667cm x 5.64444cm
breadboards: 1

parts:
  U1 = NodeMCU V1.0
  R1 = Resistor [tolerance=±5% resistance=220 package=THT]
  Part1 = KY-015 Temperature & Humidity Sensor Module [package="Breakout board"]
  Part2 = KY-006 Passive Buzzer Module [package="Breakout board"]
  LED1 = LED - 5mm [color="Red (633nm)" package="5 mm [THT]"]

nets:
  N1: U1.D1, Part1.Vin
  N2: U1.D2, Part2.S
  N3: U1.D3, R1.Pin_1
  N4: U1.3V3, Part1.S
  N5: U1.GND, Part1.-, Part2.-, LED1.cathode
  N6: R1.Pin_0, LED1.anode

custom parts:
  NodeMCU V1.0: ESP8266 based NodeMCU
  KY-015 Temperature & Humidity Sensor Module: KY-015 temperature and humidity sensor module, provides a low-latency serial interface to measure humidity and temperature.
  KY-006 Passive Buzzer Module: Passive Piezoelectric Buzzer Module Keyes KY-006, it can produce a range of sound tones depending on the input frequency.
